# Fritzing sketch wk5-ohms-law (saved by Fritzing 0.9.9b)
breadboards: 1

parts:
  R1 = Resistor [tolerance=±5% power=0.25 resistance=220 package=THT]
  V1_(9V) = BC9VPC [package=bc9vpc]
  AM1 = Multimeter (DC Current)

nets:
  N1: R1.Pin_0, AM1.COM_Probe
  N2: R1.Pin_1, V1_(9V).V-
  N3: V1_(9V).V+, AM1.A_Probe
