# Fritzing sketch wk5-led_2 (saved by Fritzing 0.9.9b)
breadboards: 1

parts:
  R1 = Resistor [tolerance=±5% power=0.25 resistance=220 package=THT]
  V1 = BC9VPC [package=bc9vpc]
  LED1 = smd LED [color="Red (633nm)" package="0805 [SMD]"]
  VM1 = Multimeter (DC Voltage)

nets:
  N1: R1.Pin_0, LED1.cathode, VM1.V_Probe
  N2: R1.Pin_1, V1.V-, VM1.COM_Probe
  N3: V1.V+, LED1.anode
